# Fritzing sketch i2cPWMDriver_servo (saved by Fritzing 0.8.7b)
breadboards: 1

parts:
  Part1 = 16-Channel 12-bit PWM Servo Driver - I2C [part_number=815]
  Part2 = Arduino Uno (Rev3)
  J1 = Basic Servo  # not connected
  J2 = Basic Servo
  J3 = Basic Servo
  J4 = Basic Servo
  Part3 = Black Joystick KY-023
  S1 = Pushbutton [package="[THT]"]
  YwRobot_Power_Supply1 = YwRobot Breadboard Power Supply [part_number=545043]  # not connected

nets:
  GND: Part1.GND, Part2.GND, J2.gnd, J3.gnd, J4.gnd, Part3.GND, S1.Pin_3, S1.Pin_4
  N1: Part1.PWM2, J2.pulse
  VCC: Part1.5.0V, J2.vcc, J3.vcc, J4.vcc
  N2: Part1.PWM1, J4.pulse
  N3: Part1.PWM0, J3.pulse
  VCC_2: Part1.VCC, Part2.5V, Part3.+5V
  N4: Part1.SDA, Part2.A4/SDA
  N5: Part1.SCL, Part2.A5/SCL
  N6: Part2.A0, Part3.VRx
  N7: Part2.A1, Part3.VRy
  N8: Part2.D8, Part3.SW
  N9: Part2.D7, S1.Pin_1, S1.Pin_2

custom parts:
  16-Channel 12-bit PWM Servo Driver - I2C: You want to make a cool robot, maybe a hexapod walker, or maybe just a piece of art with a lot of moving parts. Or maybe you want to drive a lot of LEDs with precise PWM output. Using only two pins, control 16 free-running PWM outputs! You can even chain up 62 breakouts to control up to 992 PWM outputs.
  Black Joystick KY-023: Description: The joystick is a combination of 2 analoog potentiometer and a digital switch. Arduino GND --> Module pin - Arduino +5V --> Module pin +5V Arduino Analoog 0 --> Module VRx Arduino Analoog 1 --> Module VRy Arduino Digital --> Module SW Dimensions: 1" x 1.25"
  YwRobot Breadboard Power Supply: The YwRobot Breadboard Power Supply (MB-V2) has two power rails; they can be 5V or 3V3. Power to the module can be provided through the female USB socket or through the A10 (female) 2.1mm power jack.
