# Fritzing sketch servodirect (saved by Fritzing 0.8.7b)
breadboards: 1

parts:
  Part1 = Arduino Uno (Rev3)
  J1 = Basic Servo
  J2 = Basic Servo
  J3 = Basic Servo
  J4 = Basic Servo
  Part2 = Black Joystick KY-023
  S1 = Pushbutton [package="[THT]"]

nets:
  N1: Part1.A0, Part2.VRx
  N2: Part1.A1, Part2.VRy
  N3: Part1.D8, Part2.SW
  N4: Part1.D9_PWM, J3.pulse
  N5: Part1.D10_PWM/SS, J2.pulse
  N6: Part1.D11_PWM/MOSI, J1.pulse
  N7: Part1.D6_PWM, J4.pulse
  N8: Part1.D7, S1.Pin_1, S1.Pin_2
  VCC: Part1.5V, J1.vcc, J2.vcc, J3.vcc, J4.vcc, Part2.+5V
  GND: Part1.GND, J1.gnd, J2.gnd, J3.gnd, J4.gnd, Part2.GND, S1.Pin_3, S1.Pin_4

custom parts:
  Black Joystick KY-023: Description: The joystick is a combination of 2 analoog potentiometer and a digital switch. Arduino GND --> Module pin - Arduino +5V --> Module pin +5V Arduino Analoog 0 --> Module VRx Arduino Analoog 1 --> Module VRy Arduino Digital --> Module SW Dimensions: 1" x 1.25"
